// Logisim project alu.circ as structural Verilog: 1 circuit, main circuit alu
module alu (
  input  [31:0] A,
  input  [31:0] B,
  input  [3:0] ALUSel,
  output [31:0] Result
);

  wire comparator_1_eq, comparator_2_lt, comparator_3_eq, comparator_4_eq;
  wire [1:0] signBA;
  wire [4:0] bit_extender_1_out, bit_extender_2_out, bit_extender_3_out;
  wire [6:0] bitadder_1_out;
  wire [31:0] add, adder_2_out, and1, and_2_out, and_3_out, cnto, divider_1_out, divider_2_rem, divu, mulh,
       mulh_nn, mulh_np, mulh_pn, mulhu, mult, multiplier_2_cout, multiplier_3_cout, multiplier_4_cout, or1,
       remu, shifter_4_out, shifter_5_out, sir, sll1, slt, sra1, srl1, sub, subtractor_4_out, xor1;

  Divider #(.width(32)) divider_1 (.a(A), .b(B), .out(divider_1_out));  // open: upper, rem
  Comparator #(.width(32)) comparator_1 (.a(B), .b({32{1'b0}}), .eq(comparator_1_eq));  // open: gt, lt
  Bit_Extender #(.in_width(32), .out_width(5)) bit_extender_1 (.in(B), .out(bit_extender_1_out));
  Bit_Extender #(.in_width(32), .out_width(5)) bit_extender_2 (.in(B), .out(bit_extender_2_out));
  Bit_Extender #(.in_width(32), .out_width(5)) bit_extender_3 (.in(B), .out(bit_extender_3_out));
  Adder #(.width(32)) adder_1 (.a(A), .b(B), .out(add));  // open: cin, cout
  Subtractor #(.width(32)) subtractor_1 (.a(A), .b(B), .out(sub));  // open: bin, bout
  Shifter #(.width(32), .shift("lr")) shifter_1 (.in(A), .\dist (bit_extender_1_out), .out(srl1));
  Shifter #(.width(32), .shift("ar")) shifter_2 (.in(A), .\dist (bit_extender_2_out), .out(sra1));
  Shifter #(.width(32)) shifter_3 (.in(A), .\dist (bit_extender_3_out), .out(sll1));
  Multiplexer #(.width(32), .enable("false")) multiplexer_1 (
    .in0(divider_1_out), .in1(A), .out(divu), .sel(comparator_1_eq));
  Multiplier #(.width(32)) multiplier_1 (.a(A), .b(B), .out(mult), .cout(mulhu));  // open: cin
  Multiplexer #(.select(2), .width(32), .enable("false")) multiplexer_2 (
    .in0(mulhu), .in1(mulh_np), .in2(mulh_pn), .in3(mulh_nn), .out(mulh), .sel(signBA));
  assign and1 = A & B;  // AND_Gate and_1, 32 bits wide
  assign or1 = A | B;  // OR_Gate or_1, 32 bits wide
  assign xor1 = A ^ B;  // XOR_Gate xor_1, 32 bits wide
  Comparator #(.width(32)) comparator_2 (.a(A), .b(B), .lt(comparator_2_lt));  // open: gt, eq
  BitAdder #(.width(32)) bitadder_1 (.in0(A), .in1(B), .out(bitadder_1_out));
  Multiplier #(.width(32)) multiplier_2 (.a(A), .b(B), .cout(multiplier_2_cout));  // open: out, cin
  assign slt = {{31{1'b0}}, comparator_2_lt};  // Bit_Extender bit_extender_4
  assign cnto = {{25{1'b0}}, bitadder_1_out};  // Bit_Extender bit_extender_5
  assign and_2_out = 32'h80000000 & A;  // AND_Gate and_2, 32 bits wide
  assign and_3_out = B & 32'h80000000;  // AND_Gate and_3, 32 bits wide
  Subtractor #(.width(32)) subtractor_2 (.a(multiplier_2_cout), .b(B), .out(mulh_np));  // open: bin, bout
  Shifter #(.width(32), .shift("lr")) shifter_4 (.in(and_2_out), .\dist ({5{1'b1}}), .out(shifter_4_out));
  Shifter #(.width(32), .shift("lr")) shifter_5 (.in(and_3_out), .\dist (5'b11110), .out(shifter_5_out));
  Comparator #(.width(32)) comparator_3 (
    .a(A),
    .b({B[0], B[1], B[2], B[3], B[4], B[5], B[6], B[7], B[8], B[9], B[10], B[11], B[12], B[13], B[14], B[15], B[16], B[17], B[18], B[19], B[20], B[21], B[22], B[23], B[24], B[25], B[26], B[27], B[28], B[29], B[30], B[31]}),
    .eq(comparator_3_eq));  // open: gt, lt
  Adder #(.width(32)) adder_2 (.a(shifter_4_out), .b(shifter_5_out), .out(adder_2_out));  // open: cin, cout
  Multiplier #(.width(32)) multiplier_3 (.a(A), .b(B), .cout(multiplier_3_cout));  // open: out, cin
  assign sir = {{31{1'b0}}, comparator_3_eq};  // Bit_Extender bit_extender_6
  Bit_Extender #(.in_width(32), .out_width(2), .\type ("zero")) bit_extender_7 (.in(adder_2_out), .out(signBA));
  Subtractor #(.width(32)) subtractor_3 (.a(multiplier_3_cout), .b(A), .out(mulh_pn));  // open: bin, bout
  Multiplexer #(.select(4), .width(32), .enable("false")) multiplexer_3 (
    .in0(and1), .in1(or1), .in2(xor1), .in3(add), .in4(sub), .in5(mult), .in6(mulhu), .in7(mulh), .in8(divu),
    .in9(remu), .in10(srl1), .in11(sra1), .in12(sll1), .in13(slt), .in14(cnto), .in15(sir), .out(Result),
    .sel(ALUSel));
  Divider #(.width(32)) divider_2 (.a(A), .b(B), .rem(divider_2_rem));  // open: out, upper
  Comparator #(.width(32)) comparator_4 (.a(B), .b({32{1'b0}}), .eq(comparator_4_eq));  // open: gt, lt
  Multiplier #(.width(32)) multiplier_4 (.a(A), .b(B), .cout(multiplier_4_cout));  // open: out, cin
  Subtractor #(.width(32)) subtractor_4 (.a(multiplier_4_cout), .b(A), .out(subtractor_4_out));  // open: bin, bout
  Subtractor #(.width(32)) subtractor_5 (.a(subtractor_4_out), .b(B), .out(mulh_nn));  // open: bin, bout
  Multiplexer #(.width(32), .enable("false")) multiplexer_4 (
    .in0(divider_2_rem), .in1(A), .out(remu), .sel(comparator_4_eq));

  // Notes on the sheet:
  //   INPUTS to your circuit
  //   DON'T CHANGE THE LOCATIONS OF THE INPUTS AND OUTPUTS!
  //   contributor: Youch
  //   OUTPUT from your circuit
endmodule
