// Logisim project cpu.circ as structural Verilog: 6 circuits, main circuit main
module main (
  input  [31:0] INSTRUCTION,
  input  CLOCK,
  output [31:0] FETCH_ADDRESS,
  output [31:0] ra,
  output [31:0] sp,
  output [31:0] t0,
  output [31:0] t1,
  output [31:0] t2,
  output [31:0] s0,
  output [31:0] s1,
  output [31:0] a0
);

  wire ASel, BrEq, BrLt, BrUn, BSel, lbu, lh, lhu, lui, lw, MemRW, PCsel, RegWEn;
  wire [1:0] WBSel;
  wire [2:0] ImmSel;
  wire [3:0] ALUSel;
  wire [4:0] instructiondecode_1_inst_11_7, instructiondecode_1_inst_19_15, instructiondecode_1_inst_24_20;
  wire [31:0] adder_1_out, adder_2_out, alures, immgen_1_imm, inst_31_0, instructiondecode_1_inst_imm,
       main_1_readdata, memdata_1_outputdata, multiplexer_1_out, multiplexer_2_out, multiplexer_3_out,
       multiplexer_4_out, multiplexer_5_out, PC_q, RegFile_read_data_1, RegFile_read_data_2, register_2_q,
       res;

  Adder #(.width(32)) adder_1 (.a(PC_q), .b(32'h4), .out(adder_1_out));  // open: cin, cout
  Multiplexer #(.width(32), .enable("false")) multiplexer_1 (
    .in0(adder_1_out), .in1(alures), .out(multiplexer_1_out), .sel(PCsel));
  Register #(.width(32)) PC (.D(multiplexer_1_out), .en(1'b1), .clk(CLOCK), .Q(PC_q));  // open: clr
  Multiplexer #(.width(32), .enable("false")) multiplexer_2 (
    .in0(INSTRUCTION), .in1(32'h13), .out(multiplexer_2_out), .sel(PCsel));
  Register #(.width(32)) register_1 (.D(multiplexer_2_out), .en(1'b1), .clk(CLOCK), .Q(inst_31_0));  // open: clr
  Shifter #(.width(32), .shift("lr")) shifter_1 (.in(PC_q), .\dist (5'b00010), .out(FETCH_ADDRESS));
  InstructionDecode instructiondecode_1 (
    .Instruction(inst_31_0), .inst_24_20(instructiondecode_1_inst_24_20),
    .inst_19_15(instructiondecode_1_inst_19_15), .inst_11_7(instructiondecode_1_inst_11_7),
    .inst_imm(instructiondecode_1_inst_imm));
  ControlLogic controllogic_1 (
    .Breq(BrEq), .Instruction(inst_31_0), .BrLt(BrLt), .lh(lh), .MemRW(MemRW), .PCSel(PCsel),
    .ImmSel(ImmSel), .lw(lw), .ASel(ASel), .WBSel(WBSel), .RegWEn(RegWEn), .lbu(lbu), .BSel(BSel),
    .ALUSel(ALUSel), .lhu(lhu), .BrUn(BrUn), .lui(lui));
  Register #(.width(32)) register_2 (.D(PC_q), .en(1'b1), .clk(CLOCK), .Q(register_2_q));  // open: clr
  ImmGen immgen_1 (.ImmSel(ImmSel), .inst_imm(instructiondecode_1_inst_imm), .imm(immgen_1_imm));
  Adder #(.width(32)) adder_2 (.a(register_2_q), .b(32'h4), .out(adder_2_out));  // open: cin, cout
  regfile_main RegFile (
    .rs2(instructiondecode_1_inst_24_20), .rd(instructiondecode_1_inst_11_7),
    .Read_Data_1(RegFile_read_data_1), .Read_Data_2(RegFile_read_data_2), .ra(ra), .sp(sp), .t0(t0), .t1(t1),
    .t2(t2), .s0(s0), .s1(s1), .a0(a0), .rs1(instructiondecode_1_inst_19_15), .Write_Data(res),
    .RegWEn(RegWEn), .clk(CLOCK));
  Multiplexer #(.width(32), .enable("false")) multiplexer_3 (
    .in0(RegFile_read_data_1), .in1(register_2_q), .out(multiplexer_3_out), .sel(ASel));
  BranchComp branchcomp_1 (
    .DataA(RegFile_read_data_1), .DataB(RegFile_read_data_2), .BrUn(BrUn), .BrEq(BrEq), .BrLt(BrLt));
  Multiplexer #(.width(32), .enable("false")) multiplexer_4 (
    .in0(RegFile_read_data_2), .in1(immgen_1_imm), .out(multiplexer_4_out), .sel(BSel));
  Multiplexer #(.width(32), .enable("false")) multiplexer_5 (
    .in0(multiplexer_3_out), .in1({32{1'b0}}), .out(multiplexer_5_out), .sel(lui));
  alu Arithmetic_Logic_Unit (.A(multiplexer_5_out), .B(multiplexer_4_out), .ALUSel(ALUSel), .Result(alures));
  mem_main main_1 (
    .WriteAddr(alures), .MemRW(MemRW), .ReadData(main_1_readdata), .clk(CLOCK),
    .WriteData(RegFile_read_data_2));
  MemData memdata_1 (
    .ReadData(main_1_readdata), .lh(lh), .lw(lw), .lbu(lbu), .lhu(lhu), .OutputData(memdata_1_outputdata));
  Multiplexer #(.select(2), .width(32), .enable("false")) multiplexer_6 (
    .in0(memdata_1_outputdata), .in1(alures), .in2(adder_2_out), .out(res), .sel(WBSel));  // open: in3

  // Other names for the same wires on the sheet: clk = CLOCK; fetch_addr[31:0] = FETCH_ADDRESS

  // Notes on the sheet:
  //   Output
  //   Inputs/Outputs from run.circ. DO NOT MOVE THESE.
  //   Inputs
  //   Inputs/Outputs from run.circ. DO NOT MOVE THESE.
endmodule

module ControlLogic (
  input  Breq,
  input  [31:0] Instruction,
  input  BrLt,
  output lh,
  output MemRW,
  output PCSel,
  output [2:0] ImmSel,
  output lw,
  output ASel,
  output [1:0] WBSel,
  output RegWEn,
  output lbu,
  output BSel,
  output [3:0] ALUSel,
  output lhu,
  output BrUn,
  output lui
);

  wire add, addi, addt, ALU, and1, andi, andt, auipc, B, beq, beq_t, bgeu, bgeu_t, blt, blt_t, bltu, bltu_t,
       bne, bne_t, comparator_10_eq, comparator_11_eq, comparator_12_eq, comparator_13_eq, comparator_14_eq,
       comparator_15_eq, comparator_16_eq, comparator_17_eq, comparator_18_eq, comparator_19_eq,
       comparator_20_eq, comparator_21_eq, comparator_22_eq, comparator_23_eq, comparator_24_eq,
       comparator_25_eq, comparator_26_eq, comparator_27_eq, comparator_28_eq, comparator_29_eq,
       comparator_30_eq, comparator_31_eq, comparator_32_eq, comparator_33_eq, comparator_34_eq,
       comparator_35_eq, comparator_36_eq, comparator_37_eq, comparator_38_eq, comparator_39_eq,
       comparator_40_eq, comparator_41_eq, comparator_42_eq, comparator_43_eq, comparator_44_eq,
       comparator_45_eq, comparator_46_eq, comparator_47_eq, comparator_48_eq, comparator_49_eq,
       comparator_50_eq, comparator_51_eq, comparator_52_eq, comparator_53_eq, comparator_54_eq,
       comparator_55_eq, comparator_56_eq, divu, I, Imm, Ioad, Itype, J, lb, mulh, mulhu, mult, not_1_out,
       not_2_out, or1, or_2_out, or_3_out, or_5_out, or_10_out, or_15_out, or_17_out, ori, ort, R, remu, S,
       sll1, slli, sllt, slt1, slti, sltt, srai, srl1, srli, srlt, sub, xor1, xori, xort;
  wire [1:0] multiplexer_13_out, multiplexer_15_out;
  wire [2:0] multiplexer_1_out, multiplexer_3_out, multiplexer_5_out, multiplexer_7_out;
  wire [3:0] multiplexer_2_out, multiplexer_4_out, multiplexer_6_out, multiplexer_8_out, multiplexer_10_out,
       multiplexer_11_out, multiplexer_12_out, multiplexer_14_out, multiplexer_16_out, multiplexer_18_out,
       multiplexer_19_out, multiplexer_20_out;

  Comparator #(.width(7), .mode("unsigned")) comparator_1 (
    .a(Instruction[6:0]), .b(7'b0110011), .eq(R));  // open: gt, lt
  Comparator #(.width(7), .mode("unsigned")) comparator_2 (
    .a(Instruction[6:0]), .b(7'b0000011), .eq(Ioad));  // open: gt, lt
  Comparator #(.width(7), .mode("unsigned")) comparator_3 (
    .a(Instruction[6:0]), .b(7'b0010011), .eq(Imm));  // open: gt, lt
  Comparator #(.width(7), .mode("unsigned")) comparator_4 (
    .a(Instruction[6:0]), .b(7'b0100011), .eq(S));  // open: gt, lt
  Comparator #(.width(7), .mode("unsigned")) comparator_5 (
    .a(Instruction[6:0]), .b(7'b1100011), .eq(B));  // open: gt, lt
  Comparator #(.width(7), .mode("unsigned")) comparator_6 (
    .a(Instruction[6:0]), .b(7'b0110111), .eq(lui));  // open: gt, lt
  Comparator #(.width(7), .mode("unsigned")) comparator_7 (
    .a(Instruction[6:0]), .b(7'b0010111), .eq(auipc));  // open: gt, lt
  Comparator #(.width(7), .mode("unsigned")) comparator_8 (
    .a(Instruction[6:0]), .b(7'b1101111), .eq(J));  // open: gt, lt
  Comparator #(.width(7), .mode("unsigned")) comparator_9 (
    .a(Instruction[6:0]), .b(7'b1100111), .eq(I));  // open: gt, lt
  not not_1 (not_1_out, Breq);
  not not_2 (not_2_out, BrLt);
  and and_1 (bne_t, bne, not_1_out);
  and and_2 (beq_t, beq, Breq);
  and and_3 (blt_t, blt, BrLt);
  and and_4 (bgeu_t, bgeu, not_2_out);
  or or_1 (ASel, beq, bne, blt, bltu, bgeu, J, auipc);
  Multiplexer #(.width(3), .enable("false")) multiplexer_1 (
    .in0(3'b000), .in1(3'b000), .out(multiplexer_1_out), .sel(Itype));
  Multiplexer #(.width(4), .enable("false")) multiplexer_2 (
    .in0(4'b0000), .in1(4'b0001), .out(multiplexer_2_out), .sel(ort));
  Multiplexer #(.width(3), .enable("false")) multiplexer_3 (
    .in0(multiplexer_1_out), .in1(3'b001), .out(multiplexer_3_out), .sel(S));
  Multiplexer #(.width(4), .enable("false")) multiplexer_4 (
    .in0(multiplexer_2_out), .in1(4'b0010), .out(multiplexer_4_out), .sel(xort));
  Comparator #(.width(3), .mode("unsigned")) comparator_10 (
    .a(Instruction[14:12]), .b(3'b000), .eq(comparator_10_eq));  // open: gt, lt
  Comparator #(.width(7), .mode("unsigned")) comparator_11 (
    .a(Instruction[31:25]), .b({7{1'b0}}), .eq(comparator_11_eq));  // open: gt, lt
  Comparator #(.width(3), .mode("unsigned")) comparator_12 (
    .a(Instruction[14:12]), .b(3'b000), .eq(comparator_12_eq));  // open: gt, lt
  Comparator #(.width(7), .mode("unsigned")) comparator_13 (
    .a(Instruction[31:25]), .b(7'b0100000), .eq(comparator_13_eq));  // open: gt, lt
  Comparator #(.width(3), .mode("unsigned")) comparator_14 (
    .a(Instruction[14:12]), .b(3'b000), .eq(comparator_14_eq));  // open: gt, lt
  Comparator #(.width(7), .mode("unsigned")) comparator_15 (
    .a(Instruction[31:25]), .b(7'b0000001), .eq(comparator_15_eq));  // open: gt, lt
  Comparator #(.width(3), .mode("unsigned")) comparator_16 (
    .a(Instruction[14:12]), .b(3'b011), .eq(comparator_16_eq));  // open: gt, lt
  Comparator #(.width(7), .mode("unsigned")) comparator_17 (
    .a(Instruction[31:25]), .b(7'b0000001), .eq(comparator_17_eq));  // open: gt, lt
  Comparator #(.width(3), .mode("unsigned")) comparator_18 (
    .a(Instruction[14:12]), .b(3'b101), .eq(comparator_18_eq));  // open: gt, lt
  Comparator #(.width(7), .mode("unsigned")) comparator_19 (
    .a(Instruction[31:25]), .b(7'b0000001), .eq(comparator_19_eq));  // open: gt, lt
  Comparator #(.width(3), .mode("unsigned")) comparator_20 (
    .a(Instruction[14:12]), .b(3'b111), .eq(comparator_20_eq));  // open: gt, lt
  Comparator #(.width(7), .mode("unsigned")) comparator_21 (
    .a(Instruction[31:25]), .b(7'b0000001), .eq(comparator_21_eq));  // open: gt, lt
  Multiplexer #(.width(3), .enable("false")) multiplexer_5 (
    .in0(multiplexer_3_out), .in1(3'b010), .out(multiplexer_5_out), .sel(B));
  Multiplexer #(.width(4), .enable("false")) multiplexer_6 (
    .in0(multiplexer_4_out), .in1(4'b0011), .out(multiplexer_6_out), .sel(addt));
  and and_5 (add, comparator_10_eq, R, comparator_11_eq);
  and and_6 (sub, comparator_12_eq, R, comparator_13_eq);
  and and_7 (mult, comparator_14_eq, R, comparator_15_eq);
  and and_8 (mulhu, comparator_16_eq, R, comparator_17_eq);
  and and_9 (divu, comparator_18_eq, R, comparator_19_eq);
  and and_10 (remu, comparator_20_eq, R, comparator_21_eq);
  not not_3 (BSel, R);
  Multiplexer #(.width(3), .enable("false")) multiplexer_7 (
    .in0(multiplexer_5_out), .in1(3'b011), .out(multiplexer_7_out), .sel(J));
  Multiplexer #(.width(4), .enable("false")) multiplexer_8 (
    .in0(multiplexer_6_out), .in1(4'b0100), .out(multiplexer_8_out), .sel(sub));
  or or_2 (or_2_out, beq, bne, blt, MemRW, bgeu, bltu);
  not not_4 (RegWEn, or_2_out);
  and and_11 (bltu_t, bltu, BrLt);
  Multiplexer #(.width(3), .enable("false")) multiplexer_9 (
    .in0(multiplexer_7_out), .in1(3'b100), .out(ImmSel), .sel(or_3_out));
  or or_3 (or_3_out, lui, auipc);
  Multiplexer #(.width(4), .enable("false")) multiplexer_10 (
    .in0(multiplexer_8_out), .in1(4'b0101), .out(multiplexer_10_out), .sel(mult));
  Comparator #(.width(3), .mode("unsigned")) comparator_22 (
    .a(Instruction[14:12]), .b(3'b001), .eq(comparator_22_eq));  // open: gt, lt
  Comparator #(.width(7), .mode("unsigned")) comparator_23 (
    .a(Instruction[31:25]), .b({7{1'b0}}), .eq(comparator_23_eq));  // open: gt, lt
  Comparator #(.width(3), .mode("unsigned")) comparator_24 (
    .a(Instruction[14:12]), .b(3'b100), .eq(comparator_24_eq));  // open: gt, lt
  Comparator #(.width(7), .mode("unsigned")) comparator_25 (
    .a(Instruction[31:25]), .b({7{1'b0}}), .eq(comparator_25_eq));  // open: gt, lt
  Comparator #(.width(3), .mode("unsigned")) comparator_26 (
    .a(Instruction[14:12]), .b(3'b010), .eq(comparator_26_eq));  // open: gt, lt
  Comparator #(.width(7), .mode("unsigned")) comparator_27 (
    .a(Instruction[31:25]), .b({7{1'b0}}), .eq(comparator_27_eq));  // open: gt, lt
  Comparator #(.width(3), .mode("unsigned")) comparator_28 (
    .a(Instruction[14:12]), .b(3'b101), .eq(comparator_28_eq));  // open: gt, lt
  Comparator #(.width(7), .mode("unsigned")) comparator_29 (
    .a(Instruction[31:25]), .b({7{1'b0}}), .eq(comparator_29_eq));  // open: gt, lt
  Comparator #(.width(3), .mode("unsigned")) comparator_30 (
    .a(Instruction[14:12]), .b(3'b110), .eq(comparator_30_eq));  // open: gt, lt
  Comparator #(.width(7), .mode("unsigned")) comparator_31 (
    .a(Instruction[31:25]), .b({7{1'b0}}), .eq(comparator_31_eq));  // open: gt, lt
  Comparator #(.width(3), .mode("unsigned")) comparator_32 (
    .a(Instruction[14:12]), .b(3'b111), .eq(comparator_32_eq));  // open: gt, lt
  Comparator #(.width(7), .mode("unsigned")) comparator_33 (
    .a(Instruction[31:25]), .b({7{1'b0}}), .eq(comparator_33_eq));  // open: gt, lt
  Multiplexer #(.width(4), .enable("false")) multiplexer_11 (
    .in0(multiplexer_10_out), .in1(4'b0110), .out(multiplexer_11_out), .sel(mulhu));
  and and_12 (sll1, comparator_22_eq, R, comparator_23_eq);
  and and_13 (xor1, comparator_24_eq, R, comparator_25_eq);
  and and_14 (slt1, comparator_26_eq, R, comparator_27_eq);
  and and_15 (srl1, comparator_28_eq, R, comparator_29_eq);
  and and_16 (or1, comparator_30_eq, R, comparator_31_eq);
  and and_17 (and1, comparator_32_eq, R, comparator_33_eq);
  or or_4 (ALU, Imm, R, or_5_out);
  or or_5 (or_5_out, lui, auipc);
  or or_6 (PCSel, beq_t, bne_t, blt_t, bgeu_t, bltu_t, J, I);
  Multiplexer #(.width(4), .enable("false")) multiplexer_12 (
    .in0(multiplexer_11_out), .in1(4'b0111), .out(multiplexer_12_out), .sel(mulh));
  or or_7 (andt, and1, andi);
  or or_8 (ort, or1, ori);
  or or_9 (xort, xor1, xori);
  Multiplexer #(.width(2), .enable("false")) multiplexer_13 (
    .in0(2'b00), .in1(2'b00), .out(multiplexer_13_out), .sel(Ioad));
  Multiplexer #(.width(4), .enable("false")) multiplexer_14 (
    .in0(multiplexer_12_out), .in1(4'b1000), .out(multiplexer_14_out), .sel(divu));
  Multiplexer #(.width(2), .enable("false")) multiplexer_15 (
    .in0(multiplexer_13_out), .in1(2'b01), .out(multiplexer_15_out), .sel(ALU));
  Multiplexer #(.width(4), .enable("false")) multiplexer_16 (
    .in0(multiplexer_14_out), .in1(4'b1001), .out(multiplexer_16_out), .sel(remu));
  Comparator #(.width(3), .mode("unsigned")) comparator_34 (
    .a(Instruction[14:12]), .b(3'b001), .eq(comparator_34_eq));  // open: gt, lt
  Comparator #(.width(3), .mode("unsigned")) comparator_35 (
    .a(Instruction[14:12]), .b(3'b010), .eq(comparator_35_eq));  // open: gt, lt
  Comparator #(.width(3), .mode("unsigned")) comparator_36 (
    .a(Instruction[14:12]), .b(3'b000), .eq(comparator_36_eq));  // open: gt, lt
  Comparator #(.width(3), .mode("unsigned")) comparator_37 (
    .a(Instruction[14:12]), .b(3'b100), .eq(comparator_37_eq));  // open: gt, lt
  Comparator #(.width(3), .mode("unsigned")) comparator_38 (
    .a(Instruction[14:12]), .b(3'b101), .eq(comparator_38_eq));  // open: gt, lt
  Comparator #(.width(3), .mode("unsigned")) comparator_39 (
    .a(Instruction[14:12]), .b(3'b001), .eq(comparator_39_eq));  // open: gt, lt
  Comparator #(.width(7), .mode("unsigned")) comparator_40 (
    .a(Instruction[31:25]), .b(7'b0000001), .eq(comparator_40_eq));  // open: gt, lt
  Multiplexer #(.width(2), .enable("false")) multiplexer_17 (
    .in0(multiplexer_15_out), .in1(2'b10), .out(WBSel), .sel(or_10_out));
  or or_10 (or_10_out, I, J);
  and and_18 (lh, comparator_34_eq, Ioad);
  and and_19 (lw, comparator_35_eq, Ioad);
  and and_20 (lb, comparator_36_eq, Ioad);
  and and_21 (lbu, comparator_37_eq, Ioad);
  and and_22 (lhu, comparator_38_eq, Ioad);
  and and_23 (mulh, comparator_39_eq, R, comparator_40_eq);
  or or_11 (Itype, Ioad, I, Imm);
  or or_12 (sltt, slt1, slti);
  or or_13 (srlt, srl1, srli);
  or or_14 (sllt, sll1, slli);
  Multiplexer #(.width(4), .enable("false")) multiplexer_18 (
    .in0(multiplexer_16_out), .in1(4'b1010), .out(multiplexer_18_out), .sel(srlt));
  Multiplexer #(.width(4), .enable("false")) multiplexer_19 (
    .in0(multiplexer_18_out), .in1(4'b1011), .out(multiplexer_19_out), .sel(srai));
  Comparator #(.width(3), .mode("unsigned")) comparator_41 (
    .a(Instruction[14:12]), .b(3'b010), .eq(comparator_41_eq));  // open: gt, lt
  Comparator #(.width(3), .mode("unsigned")) comparator_42 (
    .a(Instruction[14:12]), .b(3'b100), .eq(comparator_42_eq));  // open: gt, lt
  Comparator #(.width(3), .mode("unsigned")) comparator_43 (
    .a(Instruction[14:12]), .b(3'b101), .eq(comparator_43_eq));  // open: gt, lt
  Comparator #(.width(7), .mode("unsigned")) comparator_44 (
    .a(Instruction[31:25]), .b({7{1'b0}}), .eq(comparator_44_eq));  // open: gt, lt
  Comparator #(.width(3), .mode("unsigned")) comparator_45 (
    .a(Instruction[14:12]), .b(3'b101), .eq(comparator_45_eq));  // open: gt, lt
  Comparator #(.width(7), .mode("unsigned")) comparator_46 (
    .a(Instruction[31:25]), .b(7'b0100000), .eq(comparator_46_eq));  // open: gt, lt
  Comparator #(.width(3), .mode("unsigned")) comparator_47 (
    .a(Instruction[14:12]), .b(3'b110), .eq(comparator_47_eq));  // open: gt, lt
  Comparator #(.width(3), .mode("unsigned")) comparator_48 (
    .a(Instruction[14:12]), .b(3'b111), .eq(comparator_48_eq));  // open: gt, lt
  Comparator #(.width(3), .mode("unsigned")) comparator_49 (
    .a(Instruction[14:12]), .b(3'b000), .eq(comparator_49_eq));  // open: gt, lt
  Comparator #(.width(3), .mode("unsigned")) comparator_50 (
    .a(Instruction[14:12]), .b(3'b001), .eq(comparator_50_eq));  // open: gt, lt
  Multiplexer #(.width(4), .enable("false")) multiplexer_20 (
    .in0(multiplexer_19_out), .in1(4'b1100), .out(multiplexer_20_out), .sel(sllt));
  or or_15 (or_15_out, lui, auipc);
  Multiplexer #(.width(4), .enable("false")) multiplexer_21 (
    .in0(multiplexer_20_out), .in1(4'b1101), .out(ALUSel), .sel(sltt));
  and and_24 (slti, comparator_41_eq, Imm);
  and and_25 (xori, comparator_42_eq, Imm);
  and and_26 (srli, comparator_43_eq, Imm, comparator_44_eq);
  and and_27 (srai, comparator_45_eq, Imm, comparator_46_eq);
  and and_28 (ori, comparator_47_eq, Imm);
  and and_29 (andi, comparator_48_eq, Imm);
  and and_30 (addi, comparator_49_eq, Imm);
  and and_31 (slli, comparator_50_eq, Imm);
  or or_16 (addt, add, addi, or_15_out, B, J, I);
  Comparator #(.width(3), .mode("unsigned")) comparator_51 (
    .a(Instruction[14:12]), .b(3'b010), .eq(comparator_51_eq));  // open: gt, lt
  Comparator #(.width(3), .mode("unsigned")) comparator_52 (
    .a(Instruction[14:12]), .b(3'b000), .eq(comparator_52_eq));  // open: gt, lt
  Comparator #(.width(3), .mode("unsigned")) comparator_53 (
    .a(Instruction[14:12]), .b(3'b100), .eq(comparator_53_eq));  // open: gt, lt
  Comparator #(.width(3), .mode("unsigned")) comparator_54 (
    .a(Instruction[14:12]), .b(3'b110), .eq(comparator_54_eq));  // open: gt, lt
  Comparator #(.width(3), .mode("unsigned")) comparator_55 (
    .a(Instruction[14:12]), .b(3'b001), .eq(comparator_55_eq));  // open: gt, lt
  Comparator #(.width(3), .mode("unsigned")) comparator_56 (
    .a(Instruction[14:12]), .b(3'b111), .eq(comparator_56_eq));  // open: gt, lt
  or or_17 (or_17_out, bltu, bgeu);
  and and_32 (MemRW, comparator_51_eq, S);
  and and_33 (beq, comparator_52_eq, B);
  and and_34 (blt, comparator_53_eq, B);
  and and_35 (bltu, comparator_54_eq, B);
  and and_36 (bne, comparator_55_eq, B);
  and and_37 (bgeu, comparator_56_eq, B);
  and and_38 (BrUn, or_17_out, B);

  // Other names for the same wires on the sheet: inst_31_0[31:0] = Instruction; opcode[6:0] = Instruction[6:0];
  //   func3[2:0] = Instruction[14:12]; func7[6:0] = Instruction[31:25]; jal = J; jalr = I; sw = MemRW

  // Notes on the sheet:
  //   instrcion part
  //   sort part
  //   true part
  //   select part
endmodule

module InstructionDecode (
  input  [31:0] Instruction,
  output [4:0] inst_24_20,
  output [4:0] inst_19_15,
  output [4:0] inst_11_7,
  output [31:0] inst_imm
);

  wire [31:0] bit_extender_1_out;

  assign bit_extender_1_out = {{7{1'b0}}, Instruction[31:7]};  // Bit_Extender bit_extender_1
  Shifter #(.width(32)) shifter_1 (.in(bit_extender_1_out), .\dist (5'b00111), .out(inst_imm));

  assign inst_11_7 = Instruction[11:7];
  assign inst_19_15 = Instruction[19:15];
  assign inst_24_20 = Instruction[24:20];
endmodule

module BranchComp (
  input  [31:0] DataA,
  input  [31:0] DataB,
  input  BrUn,
  output BrEq,
  output BrLt
);

  wire comparator_1_eq, comparator_1_lt, comparator_2_eq, comparator_2_lt, not_1_out, not_2_out;

  Comparator #(.width(32)) comparator_1 (.a(DataA), .b(DataB), .eq(comparator_1_eq), .lt(comparator_1_lt));  // open: gt
  Comparator #(.width(32), .mode("unsigned")) comparator_2 (
    .a(DataA), .b(DataB), .eq(comparator_2_eq), .lt(comparator_2_lt));  // open: gt
  assign BrEq = not_1_out ? comparator_1_eq : 1'bz;  // Controlled_Buffer controlled_buffer_1
  assign BrLt = not_2_out ? comparator_1_lt : 1'bz;  // Controlled_Buffer controlled_buffer_2
  assign BrEq = BrUn ? comparator_2_eq : 1'bz;  // Controlled_Buffer controlled_buffer_3
  assign BrLt = BrUn ? comparator_2_lt : 1'bz;  // Controlled_Buffer controlled_buffer_4
  not not_1 (not_1_out, BrUn);
  not not_2 (not_2_out, BrUn);

  // Other names for the same wires on the sheet: DataAinput[31:0] = DataA; DataBinput[31:0] = DataB
endmodule

module ImmGen (
  input  [2:0] ImmSel,
  input  [31:0] inst_imm,
  output [31:0] imm
);

  wire comparator_1_eq, comparator_2_eq, comparator_3_eq, comparator_4_eq, comparator_5_eq;
  wire [31:0] B_2, I_0, J_3, S_1;

  Comparator #(.width(3), .mode("unsigned")) comparator_1 (
    .a(ImmSel), .b(3'b000), .eq(comparator_1_eq));  // open: gt, lt
  Comparator #(.width(3), .mode("unsigned")) comparator_2 (
    .a(ImmSel), .b(3'b001), .eq(comparator_2_eq));  // open: gt, lt
  Comparator #(.width(3), .mode("unsigned")) comparator_3 (
    .a(ImmSel), .b(3'b010), .eq(comparator_3_eq));  // open: gt, lt
  Comparator #(.width(3), .mode("unsigned")) comparator_4 (
    .a(ImmSel), .b(3'b011), .eq(comparator_4_eq));  // open: gt, lt
  Comparator #(.width(3), .mode("unsigned")) comparator_5 (
    .a(ImmSel), .b(3'b100), .eq(comparator_5_eq));  // open: gt, lt
  assign imm = comparator_1_eq ? I_0 : 32'bz;  // Controlled_Buffer controlled_buffer_1
  assign I_0 = {{20{inst_imm[31]}}, inst_imm[31:20]};  // Bit_Extender bit_extender_1
  assign imm = comparator_2_eq ? S_1 : 32'bz;  // Controlled_Buffer controlled_buffer_2
  assign S_1 = {{20{inst_imm[31]}}, {inst_imm[31:25], inst_imm[11:7]}};  // Bit_Extender bit_extender_2
  assign imm = comparator_3_eq ? B_2 : 32'bz;  // Controlled_Buffer controlled_buffer_3
  assign B_2 = {{19{inst_imm[31]}}, {inst_imm[31], inst_imm[7], inst_imm[30:25], inst_imm[11:8], 1'b0}};  // Bit_Extender bit_extender_3
  assign imm = comparator_4_eq ? J_3 : 32'bz;  // Controlled_Buffer controlled_buffer_4
  assign J_3 = {{19{inst_imm[31]}}, {inst_imm[31], inst_imm[20], inst_imm[30:21], 1'b0}};  // Bit_Extender bit_extender_4
  assign imm = comparator_5_eq ? {inst_imm[31:12], {12{1'b0}}} : 32'bz;  // Controlled_Buffer controlled_buffer_5

  // Other names for the same wires on the sheet: inst_31_7_0_input[31:0] = inst_imm; ImmSel_input[2:0] = ImmSel;
  //   ImmSel_output[31:0] = imm; U_4[31:12] = inst_imm[31:12]

  // Notes on the sheet:
  //   Immsel: I-0, S-1, B-2, J-3, U-4
  //   I-0
  //   S-1
  //   B-2
  //   J-3
  //   U-4
endmodule

module MemData (
  input  [31:0] ReadData,
  input  lh,
  input  lw,
  input  lbu,
  input  lhu,
  output [31:0] OutputData
);

  wire [31:0] bit_extender_1_out, bit_extender_2_out, bit_extender_3_out, bit_extender_4_out,
       multiplexer_1_out, multiplexer_2_out, multiplexer_3_out;

  assign bit_extender_1_out = {{24{1'b0}}, ReadData[7:0]};  // Bit_Extender bit_extender_1
  assign bit_extender_2_out = {{24{ReadData[7]}}, ReadData[7:0]};  // Bit_Extender bit_extender_2
  assign bit_extender_3_out = {{16{ReadData[15]}}, ReadData[15:0]};  // Bit_Extender bit_extender_3
  assign bit_extender_4_out = {{16{1'b0}}, ReadData[15:0]};  // Bit_Extender bit_extender_4
  Multiplexer #(.width(32), .enable("false")) multiplexer_1 (
    .in0(bit_extender_2_out), .in1(bit_extender_3_out), .out(multiplexer_1_out), .sel(lh));
  Multiplexer #(.width(32), .enable("false")) multiplexer_2 (
    .in0(multiplexer_1_out), .in1(ReadData), .out(multiplexer_2_out), .sel(lw));
  Multiplexer #(.width(32), .enable("false")) multiplexer_3 (
    .in0(multiplexer_2_out), .in1(bit_extender_1_out), .out(multiplexer_3_out), .sel(lbu));
  Multiplexer #(.width(32), .enable("false")) multiplexer_4 (
    .in0(multiplexer_3_out), .in1(bit_extender_4_out), .out(OutputData), .sel(lhu));
endmodule
